# Fritzing sketch sensors (saved by Fritzing 0.9.3b)
breadboards: 1
perfboards: 1

parts:
  Part2 = Arduino Nano (Rev3.0)
  R1 = Resistor [tolerance=±5% resistance=10k package=THT]
  Part3 = Arduino Nano (Rev3.0)
  J1 = male pin header, 4 pins [form="♂ (male)" part_number=Windgauge]
  Raspberry_Pi_Zero1 = Raspberry Pi Zero
  Raspberry_Pi_1 = Raspberry Pi 3 [part_number=RPI-3-V1.2]
  J2 = male pin header, 1 pin [form="♂ (male)"]
  J3 = male pin header, 1 pin [form="♂ (male)"]
  J4 = male pin header, 2 pins [form="♂ (male)"]
  R2 = Resistor [tolerance=±5% resistance=10k package=THT]
  J5 = male pin header, 4 pins [form="♂ (male)" part_number=Windgauge]

nets:
  GND: Part2.GND, J1.pin1, J1.pin2, Raspberry_Pi_Zero1.GND
  N1: Part2.D2, J1.pin3
  5V: Part2.5V, R1.Pin_1, Raspberry_Pi_Zero1.5V
  N2: Part2.A5, Raspberry_Pi_Zero1.GPIO3
  N3: Part2.A4, Raspberry_Pi_Zero1.GPIO2
  N4: Part2.A0, R1.Pin_0, J1.pin4
  N5: Part3.D2, J5.pin3
  N6: Part3.A5, Raspberry_Pi_1.GPIO3, J4.pin2
  N7: Part3.A0, R2.Pin_0, J5.pin4
  N8: Raspberry_Pi_1.GPIO2, J4.pin1
  N9: Raspberry_Pi_1.GND, J2.pin1
  N10: Raspberry_Pi_1.5V, J3.pin1

notes:
  windgauge
